# Fritzing sketch tower_arduino_rcc (saved by Fritzing 0.8.7b)
breadboards: 1

parts:
  Bauteil1 = Arduino Pro Mini v13
  IC1 = H-Bridge [package=THT]
  M1 = DC Motor
  LED1 = LED - 5mm [color="Green (570nm)" package="5 mm [THT]"]
  R1 = Resistor [tolerance=±5% resistance=220 package=THT]
  S1 = Toggle Switch [package=THT]
  VCC1 = Battery block 9V

nets:
  N1: Bauteil1.DTR, Bauteil1.D0/TX
  N2: IC1.1Y, M1.pin_2
  N3: IC1.2Y, M1.pin_1
  N4: IC1.VCC2, IC1.GND4, R1.Pin_0
  N5: IC1.VCC1, LED1.cathode, VCC1.-
  N6: LED1.anode, R1.Pin_1
  N7: S1.COM, VCC1.+

notes:
  RCC Platine
  (o) R L
  (o) B (Motor A)
  (o) F (Motor B)
  (o) VCC
  (o) GND
